# Fritzing sketch Esquema_montagem_tcc (saved by Fritzing 0.9.4)
breadboards: 2

parts:
  LED1 = LED - 5mm [color="Red (633nm)" package="5 mm [THT]"]
  Componente2 = Bluetooth HC-05 Macho  # not connected
  Componente3 = Arduino Mega ADK (Rev3)
  S1 = Pushbutton [package="[SMD]"]
  S2 = Pushbutton [package="[SMD]"]
  S3 = Pushbutton [package="[SMD]"]
  LED2 = smd LED [color="Green (570nm)" package="0603 [SMD]"]
  LED3 = smd LED [color="Yellow (585nm)" package="0603 [SMD]"]
  R1 = Resistor [tolerance=±5% resistance=10 package="0402 [SMD]"]
  R2 = Resistor [tolerance=±20% resistance=1 package="0402 [SMD]"]
  R3 = Resistor [tolerance=±5% resistance=10 package="0402 [SMD]"]
  R4 = Resistor [tolerance=±5% resistance=10 package="0402 [SMD]"]
  U1 = 2-Channel 5v Relay Shield [package=relay-2ch5v10a]
  YL-83_-_Control_Board1 = YL-83 Rain Sensor - Control Board
  YL-83_-_Detection_Board1 = YL-83 Rain Sensor - Detection Board
  R5 = Resistor [tolerance=±20% resistance=1 package="0402 [SMD]"]
  R6 = Resistor [tolerance=±20% resistance=1 package="0402 [SMD]"]
  R7 = Resistor [tolerance=±20% resistance=1 package="0402 [SMD]"]
  R8 = Resistor [tolerance=±20% resistance=1 package="0402 [SMD]"]
  R9 = Resistor [tolerance=±20% resistance=1 package="0402 [SMD]"]
  M1 = DC Motor
  U2 = LIPO-2000mAh [package=lipo-2000]
  U3 = LIPO-2000mAh [package=lipo-2000]  # not connected
  S4 = Taiway 100-SP-X-T1 SPDT Miniature Toggle Switch [part_number=100-SP-X-T1-0-0-B1-M2 package=THT]  # not connected
  S5 = Taiway 100-SP-X-T1 SPDT Miniature Toggle Switch [part_number=100-SP-X-T1-0-0-B1-M2 package=THT]  # not connected
  DHT11_1 = DHT11 module
  M2 = fc-51 [package=THT]
  HC-SR04_Sensor_2 = sensor boia last

nets:
  N1: LED1.cathode, Componente3.D9_PWM
  N2: LED1.anode, R4.Pin_0
  N3: Componente3.A0, YL-83_-_Control_Board1.AO
  GND: Componente3.GND, R1.Pin_1, R2.Pin_0, R3.Pin_1, R4.Pin_1, U1.GND, U1.K1-Off, YL-83_-_Control_Board1.GND, R5.Pin_0, R6.Pin_0, R7.Pin_0, R8.Pin_0, R9.Pin_1, U2.-, DHT11_1.GND, M2.pin2
  N4: Componente3.D13_PWM, R9.Pin_0, HC-SR04_Sensor_2.GND
  N5: Componente3.D12_PWM, M2.pin1
  N6: Componente3.D11_PWM, U1.IN2
  N7: Componente3.D10_PWM, U1.IN1
  N8: Componente3.D8_PWM, LED2.cathode
  VCC: Componente3.IOREF, Componente3.5V, S1.Pin_3, S1.Pin_4, S2.Pin_3, S2.Pin_4, S3.Pin_3, S3.Pin_4, U1.VCC, U1.K2-On, YL-83_-_Control_Board1.VCC, U2.+, DHT11_1.VCC, M2.pin3, HC-SR04_Sensor_2.VCC
  N9: Componente3.D2_PWM, LED3.cathode
  N10: Componente3.D3_PWM, R7.Pin_1
  N11: Componente3.D4_PWM, R8.Pin_1
  N12: Componente3.D5_PWM, S3.Pin_1, S3.Pin_2, R2.Pin_1
  N13: Componente3.D6_PWM, S1.Pin_1, S1.Pin_2, R6.Pin_1
  N14: Componente3.D7_PWM, S2.Pin_1, S2.Pin_2, R5.Pin_1
  N15: Componente3.D22, DHT11_1.DATA
  N16: LED2.anode, R3.Pin_0
  N17: LED3.anode, R1.Pin_0
  N18: U1.K2-Off, M1.pin_1
  N19: YL-83_-_Control_Board1.POS, YL-83_-_Detection_Board1.POS
  N20: YL-83_-_Control_Board1.NEG, YL-83_-_Detection_Board1.NEG

custom parts:
  2-Channel 5v Relay Shield: 2 Channel 5v Relay Shield w. 2x SPD-06VDC-SD-C
  YL-83 Rain Sensor - Control Board: The YL-83 is a rain sensor that has more resistance when dry and less resistance when wet. The module runs at 5V.
  YL-83 Rain Sensor - Detection Board: The YL-83 is a rain sensor that has more resistance when dry and less resistance when wet. The module runs at 5V.
  DHT11 module: DHT11 black pcb module
  sensor boia last: The HC-SR04 is an ultrasonic distance sensor. It is capable of providing measurement for ranges of 2cm to 400cm. The module operates at 5V.
